# Fritzing sketch arduino_breadboard_led (saved by Fritzing 0.9.3b)
breadboards: 1

parts:
  Composant1 = Arduino Nano (Rev3.0)
  RGB_SMD_LED1 = SMD RGB LED (WS2812) [package=5050]
  RGB_SMD_LED2 = SMD RGB LED (WS2812) [package=5050]  # not connected
  RGB_SMD_LED3 = SMD RGB LED (WS2812) [package=5050]  # not connected
  RGB_SMD_LED4 = SMD RGB LED (WS2812) [package=5050]  # not connected
  RGB_SMD_LED5 = SMD RGB LED (WS2812) [package=5050]  # not connected
  RGB_SMD_LED6 = SMD RGB LED (WS2812) [package=5050]  # not connected
  RGB_SMD_LED7 = SMD RGB LED (WS2812) [package=5050]  # not connected
  S1 = Momentary Switch [package=ksa_sealed_tac_switch]
  S2 = Momentary Switch [package=ksa_sealed_tac_switch]
  S3 = Momentary Switch [package=ksa_sealed_tac_switch]
  R1 = Resistor [tolerance=±5% resistance=220 package="2010 [SMD]"]
  R2 = Resistor [tolerance=±5% resistance=220 package="2010 [SMD]"]
  R3 = Resistor [tolerance=±5% resistance=220 package="2010 [SMD]"]
  VCC1 = 4 x AAA Battery Mount

nets:
  N1: Composant1.GND, RGB_SMD_LED1.DOut, R1.Pin_0, R2.Pin_0, R3.Pin_0, VCC1.-
  N2: Composant1.D2, S1.2
  N3: Composant1.D3, S2.2
  N4: Composant1.D4, S3.1, S3.2
  N5: Composant1.D5, RGB_SMD_LED1.DIn
  N6: S3.3, S3.4, R1.Pin_1
